// Logisim project Comp. Sim. PCL.circ as structural Verilog: 7 circuits, main circuit Contador de Programa
module Computador_Simulado (
  output [4:0] out_1,
  output [7:0] out_2,
  output [1:0] out_3,
  output [7:0] out_4,
  output [7:0] out_5,
  output [7:0] out_6,
  output [7:0] out_7,
  output [7:0] out_8,
  output [3:0] out_9,
  output [1:0] out_10,
  output out_11,
  output [7:0] out_12,
  output [7:0] out_13,
  output [3:0] out_14,
  output [1:0] out_15,
  output [1:0] out_16
);

  wire ADD, clock_1_out, CPU_Clock, HLT, Main_Clock, MOV_Ry, not_1_out, RAM_Clock, RAM_in, RAM_out;

  Clock clock_1 (.out(clock_1_out));
  assign Main_Clock = not_1_out ? clock_1_out : 1'bz;  // Controlled_Buffer controlled_buffer_1
  not not_1 (not_1_out, HLT);
  Sincronizador sincronizador_1 (
    .Clock(Main_Clock), .ADD(ADD), .MOV_Ry(MOV_Ry), .MOV_Ra(out_11), .RAM_out(RAM_out), .RAM_in(RAM_in),
    .RAM_Clock(RAM_Clock), .CPU_Clock(CPU_Clock));
  Central_de_Processamento central_de_processamento_1 (
    .Clock(CPU_Clock), .MOV_Ry(MOV_Ry), .MOV_RA(out_11), .Add(ADD), .RAM_Input(out_8), .Rx(out_5), .Ry(out_6));
  Contador_de_Programa contador_de_programa_1 (.Contador(out_1), .Clock(Main_Clock));
  \Decodificador_de_Instrução  \decodificador_de_instrução_1  (
    .Operador(out_9), .ADD(ADD), .RAM_in(RAM_in), .MOV_Ra(out_11), .RAM_out(RAM_out), .HLT(HLT),
    .MOV_Ry(MOV_Ry));
  ROM #(.addrWidth(5)) rom_1 (.addr(out_1), .data(out_2));  // open: sel
  RAM #(.addrWidth(2), .bus("separate")) ram_1 (
    .addr(out_3), .din(out_8), .data(out_4), .str(RAM_in), .clk(RAM_Clock), .ld(RAM_out));  // open: sel, clr
  Carteiro carteiro_1 (.\Endereço_de_Registrador (out_10), .Dados_da_RAM(out_4), .Rx(out_5), .Ry(out_6));
  \Reg__de_Instrução  \reg_de_instrução_1  (
    .Dados_da_ROM(out_2), .Clock(Main_Clock), .\Endereço_RAM (out_3), .\Endereço_de_Registrador (out_10),
    .Operador(out_9));

  assign out_12 = out_4;
  assign out_13 = out_2;
  assign out_14 = out_9;
  assign out_15 = out_10;
  assign out_16 = out_3;

  // Other names for the same wires on the sheet: Contador_de_Programa[4:0] = out_1; Dados_da_RAM[7:0] = out_4;
  //   Dados_da_ROM[7:0] = out_2; Endereço_de_Registrador[1:0] = out_10; Endereço_RAM[1:0] = out_3; MOV_Ra = out_11;
  //   Operador[3:0] = out_9; Ra[7:0] = out_7; RAM_Input[7:0] = out_8; Rx[7:0] = out_5; Ry[7:0] = out_6

  // Notes on the sheet:
  //   Lista de Instruções
  //   contents of rom_1 (hex, n*v repeats v):
  //   0 b1 b4 d8 19 df c7 f0
endmodule

// PC
module Contador_de_Programa (
  input  Clock,
  output [4:0] Contador
);

  Counter #(.width(5), .max('h1f)) counter_1 (.Q(Contador), .clk(Clock));  // open: load, D, count, carry, clr

  // Notes on the sheet:
  //   Contador de Programa
endmodule

// Rg. Instr.
module \Reg__de_Instrução  (
  input  [7:0] Dados_da_ROM,
  input  Clock,
  output [1:0] \Endereço_RAM ,
  output [1:0] \Endereço_de_Registrador ,
  output [3:0] Operador
);

  Register register_1 (
    .D(Dados_da_ROM), .Q({Operador, \Endereço_de_Registrador , \Endereço_RAM }), .clk(Clock));  // open: en, clr

  // Notes on the sheet:
  //   Registrador de Instruções
  //   Separando em pedaços
endmodule

// Instr. Decoder
module \Decodificador_de_Instrução  (
  input  [3:0] Operador,
  output ADD,
  output HLT,
  output MOV_Ry,
  output MOV_Ra,
  output RAM_out,
  output RAM_in
);

  and _1001 (ADD, Operador[0], ~Operador[1], ~Operador[2], Operador[3]);  // AND_Gate
  and _1000 (HLT, ~Operador[0], ~Operador[1], ~Operador[2], Operador[3]);  // AND_Gate
  and _1011 (MOV_Ry, Operador[0], Operador[1], ~Operador[2], Operador[3]);  // AND_Gate
  and _1100 (MOV_Ra, ~Operador[0], ~Operador[1], Operador[2], Operador[3]);  // AND_Gate
  and _1101 (RAM_out, Operador[0], ~Operador[1], Operador[2], Operador[3]);  // AND_Gate
  and _1110 (RAM_in, ~Operador[0], Operador[1], Operador[2], Operador[3]);  // AND_Gate

  // Notes on the sheet:
  //   Decodificador de Instrução
endmodule

module Carteiro (
  input  [1:0] \Endereço_de_Registrador ,
  input  [7:0] Dados_da_RAM,
  output [7:0] Rx,
  output [7:0] Ry
);

  wire _00_out, _11_out;

  and _00 (_00_out, ~\Endereço_de_Registrador [0], ~\Endereço_de_Registrador [1]);  // AND_Gate
  and _11 (_11_out, \Endereço_de_Registrador [0], \Endereço_de_Registrador [1]);
  assign Rx = _00_out ? Dados_da_RAM : 8'bz;  // Controlled_Buffer controlled_buffer_1
  assign Ry = _11_out ? Dados_da_RAM : 8'bz;  // Controlled_Buffer controlled_buffer_2

  // Notes on the sheet:
  //   Carteiro
endmodule

// C.P.U
module Central_de_Processamento (
  input  [7:0] Rx,
  input  [7:0] Ry,
  input  Clock,
  input  MOV_Ry,
  input  MOV_RA,
  input  Add,
  output [7:0] RAM_Input
);

  wire MOV_RA_t, MOV_Rx, not_1_out, not_2_out;
  wire [7:0] adder_1_out, controlled_buffer_1_out, controlled_buffer_4_out, Input_Rx, Rx_q, Ry_q;

  assign controlled_buffer_1_out = not_2_out ? Rx : 8'bz;  // Controlled_Buffer controlled_buffer_1
  not not_1 (not_1_out, MOV_RA_t);
  not not_2 (not_2_out, MOV_Rx);
  assign Input_Rx = not_1_out ? controlled_buffer_1_out : 8'bz;  // Controlled_Buffer controlled_buffer_2
  Register u_Rx (.D(Input_Rx), .Q(Rx_q), .clk(Clock));  // open: en, clr
  Register u_Ry (.D(Ry), .Q(Ry_q), .clk(Clock));  // open: en, clr
  Adder adder_1 (.a(Rx_q), .b(Ry_q), .out(adder_1_out));  // open: cin, cout
  assign Input_Rx = MOV_Ry ? Ry_q : 8'bz;  // Controlled_Buffer controlled_buffer_3
  assign controlled_buffer_4_out = Add ? adder_1_out : 8'bz;  // Controlled_Buffer controlled_buffer_4
  Register RA (.D(controlled_buffer_4_out), .Q(RAM_Input), .clk(Clock));  // open: en, clr
  assign Input_Rx = MOV_RA ? RAM_Input : 8'bz;  // Controlled_Buffer controlled_buffer_5

  // Other names for the same wires on the sheet: Ra[7:0] = RAM_Input

  // Notes on the sheet:
  //   Painel de Entradas
endmodule

// Sinc.
module Sincronizador (
  input  Clock,
  input  ADD,
  input  MOV_Ry,
  input  MOV_Ra,
  input  RAM_out,
  input  RAM_in,
  output CPU_Clock,
  output RAM_Clock
);

  wire and_1_out, and_2_out, and_3_out, and_4_out, and_5_out;

  and and_1 (and_1_out, ADD, Clock);
  and and_2 (and_2_out, MOV_Ry, Clock);
  and and_3 (and_3_out, MOV_Ra, Clock);
  and and_4 (and_4_out, RAM_out, Clock);
  and and_5 (and_5_out, RAM_in, Clock);
  or or_1 (CPU_Clock, and_1_out, and_2_out, and_3_out);
  or or_2 (RAM_Clock, and_4_out, and_5_out);

  // Notes on the sheet:
  //   SINCRONIZADOR
endmodule
