// Logisim project Comp. Sim. PCL.circ as structural Verilog: 8 circuits, main circuit Contador de Programa
module Computador_Simulado (
  input  Clear,
  output [4:0] out_2,
  output [7:0] out_3,
  output [7:0] out_4,
  output [1:0] out_5,
  output [7:0] out_6,
  output [7:0] out_7,
  output [7:0] out_8,
  output [7:0] out_9,
  output [3:0] out_10,
  output [1:0] out_11,
  output [7:0] out_12,
  output [7:0] out_13,
  output [3:0] out_14,
  output [1:0] out_15,
  output [1:0] out_16
);

  wire ADD, clock_1_out, CPU_Clock, HLT, Main_Clock, MOV_Ra, MOV_Ry, not_1_out, RAM_Clock, RAM_in, RAM_out;

  assign Main_Clock = not_1_out ? clock_1_out : 1'bz;  // Controlled_Buffer controlled_buffer_1
  Clock clock_1 (.out(clock_1_out));
  not not_1 (not_1_out, HLT);
  Sincronizador sincronizador_1 (
    .Clock(Main_Clock), .ADD(ADD), .MOV_Ry(MOV_Ry), .MOV_Ra(MOV_Ra), .RAM_out(RAM_out), .RAM_in(RAM_in),
    .RAM_Clock(RAM_Clock), .CPU_Clock(CPU_Clock));
  Central_de_Processamento central_de_processamento_1 (
    .CPU_Clock(CPU_Clock), .MOV_Ry(MOV_Ry), .MOV_RA(MOV_Ra), .Add(ADD), .Ry(out_6), .Clear(Clear),
    .RAM_Clock(RAM_Clock), .RAM_in(RAM_in), .RAM_Input(out_9));
  Contador_de_Programa contador_de_programa_1 (.Contador(out_2), .Clock(Main_Clock), .Clear(Clear));
  \Decodificador_de_Instrução  \decodificador_de_instrução_1  (
    .Operador(out_10), .ADD(ADD), .RAM_in(RAM_in), .MOV_Ra(MOV_Ra), .RAM_out(RAM_out), .HLT(HLT),
    .MOV_Ry(MOV_Ry));
  ROM #(.addrWidth(5)) rom_1 (.addr(out_2), .data(out_4));  // open: sel
  RAM #(.addrWidth(2), .bus("separate")) ram_1 (
    .addr(out_5), .din(out_9), .data(out_8), .str(RAM_in), .clk(RAM_Clock), .ld(RAM_out));  // open: sel, clr
  \Reg__de_Instrução  \reg_de_instrução_1  (
    .Dados_da_ROM(out_4), .Clock(Main_Clock), .\Endereço_RAM (out_5), .\Endereço_de_Registrador (out_11),
    .Operador(out_10), .Clear(Clear));
  Banco_de_Registradores banco_de_registradores_1 (
    .RAM_Clock(RAM_Clock), .Clear(Clear), .RAM_out(RAM_out), .\Endereço_RAM (out_5),
    .\Endereço_de_Registrador (out_11), .Dados_da_RAM(out_8), .Ry(out_6));

  assign out_12 = out_8;
  assign out_13 = out_4;
  assign out_14 = out_10;
  assign out_15 = out_11;
  assign out_16 = out_5;

  // Other names for the same wires on the sheet: Contador_de_Programa[4:0] = out_2; Dados_da_RAM[7:0] = out_8;
  //   Dados_da_ROM[7:0] = out_4; Endereço_de_Registrador[1:0] = out_11; Endereço_RAM[1:0] = out_5;
  //   Operador[3:0] = out_10; Ra[7:0] = out_7; RAM_Input[7:0] = out_9; Rx[7:0] = out_3; Ry[7:0] = out_6

  // Notes on the sheet:
  //   COMPUTADOR SIMULADO CRIADO POR:
  //    NIVALDO DA SILVA FREITAS NETO
  //   contents of rom_1 (hex, n*v repeats v):
  //   d0 b0 d5 95 c0 da 98 c0 df 9c e0 80
endmodule

// PC
module Contador_de_Programa (
  input  Clear,
  input  Clock,
  output [4:0] Contador
);

  Counter #(.width(5), .max('h1f)) counter_1 (.Q(Contador), .clk(Clock), .clr(Clear));  // open: load, D, count, carry

  // Notes on the sheet:
  //   Contador de Programa
endmodule

// Rg. Instr.
module \Reg__de_Instrução  (
  input  [7:0] Dados_da_ROM,
  input  Clock,
  input  Clear,
  output [1:0] \Endereço_RAM ,
  output [1:0] \Endereço_de_Registrador ,
  output [3:0] Operador
);

  Register register_1 (
    .D(Dados_da_ROM), .Q({Operador, \Endereço_de_Registrador , \Endereço_RAM }), .clk(Clock), .clr(Clear));  // open: en

  // Notes on the sheet:
  //   Registrador de Instruções
  //   Separando em pedaços
endmodule

// Instr. Decoder
module \Decodificador_de_Instrução  (
  input  [3:0] Operador,
  output ADD,
  output HLT,
  output MOV_Ry,
  output MOV_Ra,
  output RAM_out,
  output RAM_in
);

  and _1001 (ADD, Operador[0], ~Operador[1], ~Operador[2], Operador[3]);  // AND_Gate
  and _1000 (HLT, ~Operador[0], ~Operador[1], ~Operador[2], Operador[3]);  // AND_Gate
  and _1011 (MOV_Ry, Operador[0], Operador[1], ~Operador[2], Operador[3]);  // AND_Gate
  and _1100 (MOV_Ra, ~Operador[0], ~Operador[1], Operador[2], Operador[3]);  // AND_Gate
  and _1101 (RAM_out, Operador[0], ~Operador[1], Operador[2], Operador[3]);  // AND_Gate
  and _1110 (RAM_in, ~Operador[0], Operador[1], Operador[2], Operador[3]);  // AND_Gate

  // Notes on the sheet:
  //   Decodificador de Instrução
endmodule

module Carteiro (
  input  [1:0] \Endereço_de_Registrador ,
  input  [7:0] Dados_da_RAM,
  output [7:0] Rx,
  output [7:0] Ry
);

  wire _00_out, _11_out;

  and _00 (_00_out, ~\Endereço_de_Registrador [0], ~\Endereço_de_Registrador [1]);  // AND_Gate
  and _11 (_11_out, \Endereço_de_Registrador [0], \Endereço_de_Registrador [1]);
  assign Rx = _00_out ? Dados_da_RAM : 8'bz;  // Controlled_Buffer controlled_buffer_1
  assign Ry = _11_out ? Dados_da_RAM : 8'bz;  // Controlled_Buffer controlled_buffer_2

  // Notes on the sheet:
  //   Carteiro
endmodule

// C.P.U
module Central_de_Processamento (
  input  [7:0] Ry,
  input  RAM_Clock,
  input  CPU_Clock,
  input  MOV_Ry,
  input  MOV_RA,
  input  Add,
  input  Clear,
  input  RAM_in,
  output [7:0] RAM_Input
);

  wire or_1_out, or_2_out;
  wire [7:0] adder_1_out, controlled_buffer_2_out, Input_Rx, Rx_q, Ry_q;

  or or_1 (or_1_out, RAM_Clock, MOV_Ry, MOV_RA);
  or or_2 (or_2_out, RAM_Clock, CPU_Clock, MOV_Ry);
  Register #(.trigger("high")) Rx (.D(Input_Rx), .Q(Rx_q), .clk(or_1_out), .clr(Clear));  // open: en
  Register #(.trigger("high")) u_Ry (.D(Ry), .Q(Ry_q), .clk(or_2_out), .clr(Clear));  // open: en
  Adder adder_1 (.a(Rx_q), .b(Ry_q), .out(adder_1_out));  // open: cin, cout
  assign Input_Rx = MOV_Ry ? Ry_q : 8'bz;  // Controlled_Buffer controlled_buffer_1
  Register RA (.D(controlled_buffer_2_out), .Q(RAM_Input), .clk(CPU_Clock), .clr(Clear));  // open: en
  assign controlled_buffer_2_out = Add ? adder_1_out : 8'bz;  // Controlled_Buffer controlled_buffer_2
  assign Input_Rx = MOV_RA ? RAM_Input : 8'bz;  // Controlled_Buffer controlled_buffer_3

  // Notes on the sheet:
  //   Painel de Entradas
endmodule

// Sinc.
module Sincronizador (
  input  Clock,
  input  ADD,
  input  MOV_Ry,
  input  MOV_Ra,
  input  RAM_out,
  input  RAM_in,
  output CPU_Clock,
  output RAM_Clock
);

  wire and_1_out, and_2_out, and_3_out, and_4_out, and_5_out;

  and and_1 (and_1_out, ADD, Clock);
  and and_2 (and_2_out, MOV_Ry, Clock);
  and and_3 (and_3_out, MOV_Ra, Clock);
  and and_4 (and_4_out, RAM_out, Clock);
  and and_5 (and_5_out, RAM_in, Clock);
  or or_1 (CPU_Clock, and_1_out, and_2_out, and_3_out);
  or or_2 (RAM_Clock, and_4_out, and_5_out);

  // Notes on the sheet:
  //   SINCRONIZADOR
endmodule

// Banco de Reg.
module Banco_de_Registradores (
  input  RAM_Clock,
  input  Clear,
  input  RAM_out,
  input  [1:0] \Endereço_RAM ,
  input  [1:0] \Endereço_de_Registrador ,
  input  [7:0] Dados_da_RAM,
  output [7:0] Ry
);

  wire and_1_out, and_2_out, and_3_out, and_4_out, decoder_1_out0, decoder_1_out1, decoder_1_out2,
       decoder_1_out3;
  wire [7:0] R0_q, R1_q, R2_q, R3_q;

  Decoder #(.select(2)) decoder_1 (
    .out0(decoder_1_out0), .out1(decoder_1_out1), .out2(decoder_1_out2), .out3(decoder_1_out3),
    .sel(\Endereço_de_Registrador ), .en(RAM_out));
  and and_1 (and_1_out, decoder_1_out0, RAM_out);
  and and_2 (and_2_out, decoder_1_out1, RAM_out);
  Register R0 (.D(Dados_da_RAM), .en(and_1_out), .Q(R0_q), .clk(RAM_Clock), .clr(Clear));
  Register R1 (.D(Dados_da_RAM), .en(and_2_out), .Q(R1_q), .clk(RAM_Clock), .clr(Clear));
  and and_3 (and_3_out, decoder_1_out2, RAM_out);
  and and_4 (and_4_out, decoder_1_out3, RAM_out);
  Register R2 (.D(Dados_da_RAM), .en(and_3_out), .Q(R2_q), .clk(RAM_Clock), .clr(Clear));
  Register R3 (.D(Dados_da_RAM), .en(and_4_out), .Q(R3_q), .clk(RAM_Clock), .clr(Clear));
  Multiplexer #(.select(2), .width(8)) multiplexer_1 (
    .in0(R0_q), .in1(R1_q), .in2(R2_q), .in3(R3_q), .out(Ry), .sel(\Endereço_de_Registrador ));  // open: en

  // Other names for the same wires on the sheet: Endereço_Rx_Ry[1:0] = \Endereço_RAM 

  // Notes on the sheet:
  //   Entradas
endmodule
